# Fritzing sketch HappyTimeSketch (saved by Fritzing 0.9.4)
breadboards: 1

parts:
  Componente1 = Arduino Nano (Rev3.0) (ICSP)
  J1 = female pin header, 4 pins [form="♀ (female)"]
  S1 = Pushbutton [package="[THT]"]
  S2 = Pushbutton [package="[THT]"]
  S3 = Pushbutton [package="[THT]"]
  S4 = Pushbutton [package="[THT]"]
  S5 = Pushbutton [package="[THT]"]
  J2 = Piezo Speaker
  VCC1 = Battery block 9V

nets:
  N1: Componente1.RESET, S5.Pin_3, S5.Pin_4
  N2: Componente1.GND, J1.pin2, S1.Pin_3, S1.Pin_4, S2.Pin_3, S2.Pin_4, S3.Pin_3, S3.Pin_4, S4.Pin_3, S4.Pin_4, VCC1.-
  N3: Componente1.D3, S1.Pin_1, S1.Pin_2
  N4: Componente1.D4, S2.Pin_1, S2.Pin_2
  N5: Componente1.D5, S3.Pin_1, S3.Pin_2
  N6: Componente1.D6, S4.Pin_1, S4.Pin_2
  N7: Componente1.D7, J2.pin1
  N8: Componente1.VIN, VCC1.+
  N9: Componente1.5V, J1.pin1, S5.Pin_1, S5.Pin_2, J2.pin2
  N10: Componente1.A5, J1.pin4
  N11: Componente1.A4, J1.pin3

notes:
  ©2021 Steven R. Loomis
  srl295@gmail.com
  github.com/srl295/happytimer
  Apache-2.0
